# Fritzing sketch SF51-Home-Power (saved by Fritzing 0.9.3b)
breadboards: 1

parts:
  Q1 = NPN-Transistor [package="SOT-23 [SMD]"]
  12_V = Power Jack [package=power_jack_pth_lock]
  U2 = RELAY-SOLIDSTATE [package=relay-s108t02]
  J1 = MAGJACK [package=magjack]
  U1 = NodeMCU V3.0
  TRXCOM1 = RJ45-TRXCOM [part_number=TRJ0011BANL]
  Q2 = NPN-Transistor [package="SOT-23 [SMD]"]
  D1 = Diode [package=diode-1n4148]
  D2 = Diode [package=diode-1n4148]
  U3 = AD22100 - Voltage Output Temperature Sensor with Signal Conditioning [part_number=AD22100]
  S3 = Pushbutton [package="[SMD]"]

nets:
  N1: Q1.2, 12_V.PWR, U1.GND#6, U1.GND#13, U1.GND#16, U1.GND#33, Q2.2
  N2: Q1.0, U1.D2
  N3: Q1.1, S3.Pin_1, S3.Pin_2, S3.Pin_3, S3.Pin_4
  N4: 12_V.GND, J1.SHIELD, D1.A
  N5: U2.T1, TRXCOM1.n.c., TRXCOM1.CHS_Ground
  N6: U2.T2, TRXCOM1.Receive_CT, TRXCOM1.Receive_RD-
  N7: U2.-, TRXCOM1.Green_Kathode_-, TRXCOM1.Green_Anode_+
  N8: J1.RD-, Q2.1
  N9: U1.D1, Q2.0
  N10: U1.Vin, U3.Vo
  N11: D1.C, D2.A
  N12: D2.C, U3.GND

custom parts:
  NodeMCU V3.0: ESP8266 based NodeMCU
